// Logisim project Logisim入门1.circ as structural Verilog
module myname (
  input  [15:0] in_1,
  input  [15:0] in_2,
  input  [15:0] in_3,
  input  [15:0] in_4,
  input  [15:0] in_5,
  input  [15:0] in_6,
  input  [15:0] in_7,
  input  [15:0] in_8,
  input  [15:0] in_9,
  input  [15:0] in_10,
  input  [15:0] in_11,
  input  [15:0] in_12,
  input  [15:0] in_13,
  input  [15:0] in_14,
  input  [15:0] in_15,
  input  [15:0] in_16,
  input  [15:0] in_17,
  input  [15:0] in_18,
  input  [15:0] in_19,
  input  [15:0] in_20,
  input  [15:0] in_21,
  input  [15:0] in_22,
  input  [15:0] in_23,
  input  [15:0] in_24,
  input  [15:0] in_25,
  input  [15:0] in_26,
  input  [15:0] in_27,
  input  [15:0] in_28,
  input  [15:0] in_29,
  input  [15:0] in_30,
  input  [15:0] in_31,
  input  [15:0] in_32,
  input  [15:0] in_33,
  input  [15:0] in_34,
  input  [15:0] in_35,
  input  [15:0] in_36,
  input  [15:0] in_37,
  input  [15:0] in_38,
  input  [15:0] in_39,
  input  [15:0] in_40,
  input  [15:0] in_41,
  input  [15:0] in_42,
  input  [15:0] in_43,
  input  [15:0] in_44,
  input  [15:0] in_45,
  input  [15:0] in_46,
  input  [15:0] in_47,
  input  [15:0] in_48
);

  DotMatrix #(.matrixcols(16), .matrixrows(16)) dotmatrix_1 (
    .col0(in_1), .col1(in_7), .col2(in_13), .col3(in_19), .col4(in_25), .col5(in_31), .col6(in_37),
    .col7(in_43), .col8(in_44), .col9(in_38), .col10(in_32), .col11(in_26), .col12(in_20), .col13(in_14),
    .col14(in_8), .col15(in_2));
  DotMatrix #(.matrixcols(16), .matrixrows(16)) dotmatrix_2 (
    .col0(in_3), .col1(in_9), .col2(in_15), .col3(in_21), .col4(in_27), .col5(in_33), .col6(in_39),
    .col7(in_45), .col8(in_46), .col9(in_40), .col10(in_34), .col11(in_28), .col12(in_22), .col13(in_16),
    .col14(in_10), .col15(in_4));
  DotMatrix #(.matrixcols(16), .matrixrows(16)) dotmatrix_3 (
    .col0(in_5), .col1(in_11), .col2(in_17), .col3(in_23), .col4(in_29), .col5(in_35), .col6(in_41),
    .col7(in_47), .col8(in_48), .col9(in_42), .col10(in_36), .col11(in_30), .col12(in_24), .col13(in_18),
    .col14(in_12), .col15(in_6));
endmodule

module mynum (
  input  in_1,
  input  in_2,
  input  in_3,
  input  in_4,
  input  in_5,
  input  in_6,
  input  in_7,
  input  in_8,
  input  in_9,
  input  in_10,
  input  in_11,
  input  in_12,
  input  in_13,
  input  in_14,
  input  in_15,
  input  in_16,
  input  in_17,
  input  in_18,
  input  in_19,
  input  in_20,
  input  in_21,
  input  in_22,
  input  in_23,
  input  in_24,
  input  in_25,
  input  in_26,
  input  in_27,
  input  in_28,
  input  in_29,
  input  in_30,
  input  in_31,
  input  in_32,
  input  in_33,
  input  in_34,
  input  in_35,
  input  in_36,
  input  in_37,
  input  in_38,
  input  in_39,
  input  in_40,
  input  in_41,
  input  in_42,
  input  in_43,
  input  in_44,
  input  in_45,
  input  in_46,
  input  in_47,
  input  in_48,
  input  in_49,
  input  in_50,
  input  in_51,
  input  in_52,
  input  in_53,
  input  in_54,
  input  in_55,
  input  in_56,
  input  in_57,
  input  in_58,
  input  in_59,
  input  in_60,
  input  in_61,
  input  in_62,
  input  in_63,
  input  in_64
);

  _7_Segment_Display u_7_segment_display_1 (
    .g(in_17), .f(in_1), .a(in_2), .b(in_18), .e(in_33), .d(in_49), .c(in_50), .dp(in_34));
  _7_Segment_Display u_7_segment_display_2 (
    .g(in_19), .f(in_3), .a(in_4), .b(in_20), .e(in_35), .d(in_51), .c(in_52), .dp(in_36));
  _7_Segment_Display u_7_segment_display_3 (
    .g(in_21), .f(in_5), .a(in_6), .b(in_22), .e(in_37), .d(in_53), .c(in_54), .dp(in_38));
  _7_Segment_Display u_7_segment_display_4 (
    .g(in_23), .f(in_7), .a(in_8), .b(in_24), .e(in_39), .d(in_55), .c(in_56), .dp(in_40));
  _7_Segment_Display u_7_segment_display_5 (
    .g(in_25), .f(in_9), .a(in_10), .b(in_26), .e(in_41), .d(in_57), .c(in_58), .dp(in_42));
  _7_Segment_Display u_7_segment_display_6 (
    .g(in_27), .f(in_11), .a(in_12), .b(in_28), .e(in_43), .d(in_59), .c(in_60), .dp(in_44));
  _7_Segment_Display u_7_segment_display_7 (
    .g(in_29), .f(in_13), .a(in_14), .b(in_30), .e(in_45), .d(in_61), .c(in_62), .dp(in_46));
  _7_Segment_Display u_7_segment_display_8 (
    .g(in_31), .f(in_15), .a(in_16), .b(in_32), .e(in_47), .d(in_63), .c(in_64), .dp(in_48));
endmodule

module T3 (
  input  in_1,
  input  in_2,
  input  in_3,
  input  in_4,
  input  in_5,
  input  in_6,
  input  in_7,
  input  in_8,
  input  in_9,
  output out_10,
  output out_11,
  output out_12,
  output out_13,
  output out_14
);

  wire transistor_3_out, transistor_6_out, transistor_12_out, transistor_16_out;

  Transistor transistor_1 (.in(1'b0), .out(out_10), .gate(in_3));
  Transistor #(.\type ("n")) transistor_2 (.in(1'b0), .out(out_13), .gate(in_8));
  Transistor #(.\type ("n")) transistor_3 (.in(1'b1), .out(transistor_3_out), .gate(in_1));
  Transistor #(.\type ("n")) transistor_4 (.in(transistor_3_out), .out(out_10), .gate(in_3));
  Transistor transistor_5 (.in(1'b0), .out(out_10), .gate(in_1));
  Transistor transistor_6 (.in(1'b1), .out(transistor_6_out), .gate(in_6));
  Transistor transistor_7 (.in(transistor_6_out), .out(out_13), .gate(in_8));
  Transistor #(.\type ("n")) transistor_8 (.in(1'b0), .out(out_13), .gate(in_6));
  Transistor #(.\type ("n")) transistor_9 (.in(1'b1), .out(out_11), .gate(in_5));
  Transistor #(.\type ("n")) transistor_10 (.in(1'b1), .out(out_11), .gate(in_2));
  Transistor transistor_11 (.in(transistor_12_out), .out(out_11), .gate(in_2));
  Transistor transistor_12 (.in(1'b0), .out(transistor_12_out), .gate(in_5));
  Transistor transistor_13 (.in(1'b1), .out(out_14), .gate(in_9));
  Transistor transistor_14 (.in(1'b1), .out(out_14), .gate(in_7));
  Transistor #(.\type ("n")) transistor_15 (.in(transistor_16_out), .out(out_14), .gate(in_7));
  Transistor #(.\type ("n")) transistor_16 (.in(1'b0), .out(transistor_16_out), .gate(in_9));
  Transistor transistor_17 (.in(1'b1), .out(out_12), .gate(in_4));
  Transistor #(.\type ("n")) transistor_18 (.in(1'b0), .out(out_12), .gate(in_4));
endmodule

module my_AND (
  input  in_1,
  input  in_2,
  output out_3
);

  wire transistor_2_out;

  Transistor transistor_1 (.in(1'b0), .out(out_3), .gate(in_2));
  Transistor #(.\type ("n")) transistor_2 (.in(1'b1), .out(transistor_2_out), .gate(in_1));
  Transistor #(.\type ("n")) transistor_3 (.in(transistor_2_out), .out(out_3), .gate(in_2));
  Transistor transistor_4 (.in(1'b0), .out(out_3), .gate(in_1));
endmodule

module my_OR (
  input  in_1,
  input  in_2,
  output out_3
);

  wire transistor_4_out;

  Transistor #(.\type ("n")) transistor_1 (.in(1'b1), .out(out_3), .gate(in_1));
  Transistor #(.\type ("n")) transistor_2 (.in(1'b1), .out(out_3), .gate(in_2));
  Transistor transistor_3 (.in(transistor_4_out), .out(out_3), .gate(in_1));
  Transistor transistor_4 (.in(1'b0), .out(transistor_4_out), .gate(in_2));
endmodule

module my_NOR (
  input  in_1,
  output out_2
);

  Transistor transistor_1 (.in(1'b1), .out(out_2), .gate(in_1));
  Transistor #(.\type ("n")) transistor_2 (.in(1'b0), .out(out_2), .gate(in_1));
endmodule

module MUX1 (
  input  in_1,
  input  in_2,
  input  in_3,
  output out_4
);

  wire and_1_out_3, and_2_out_3, nor_1_out_2;

  \nor  nor_1 (.in_1(in_1), .out_2(nor_1_out_2));
  \and  and_1 (.in_1(nor_1_out_2), .in_2(in_2), .out_3(and_1_out_3));
  \and  and_2 (.in_1(in_1), .in_2(in_3), .out_3(and_2_out_3));
  \or  or_1 (.in_1(and_1_out_3), .in_2(and_2_out_3), .out_3(out_4));
endmodule

module _2bitMUX4_1 (
  input  S2,
  input  S1,
  input  a00_0,
  input  a00_1,
  input  a10_0,
  input  a10_1,
  input  a01_0,
  input  a01_1,
  input  a11_0,
  input  a11_1,
  output L_0,
  output L_1
);

  wire mux1_1_out_4, mux1_2_out_4, mux1_3_out_4, mux1_4_out_4, nor_1_out_2, nor_2_out_2;

  \nor  nor_1 (.in_1(S1), .out_2(nor_1_out_2));
  MUX1 mux1_1 (.in_2(a00_0), .in_3(a10_0), .in_1(S1), .out_4(mux1_1_out_4));
  MUX1 mux1_2 (.in_2(a01_0), .in_3(a11_0), .in_1(S1), .out_4(mux1_2_out_4));
  MUX1 mux1_3 (.in_2(a11_1), .in_3(a01_1), .in_1(nor_1_out_2), .out_4(mux1_3_out_4));
  MUX1 mux1_4 (.in_2(a10_1), .in_3(a00_1), .in_1(nor_1_out_2), .out_4(mux1_4_out_4));
  MUX1 mux1_5 (.in_2(mux1_1_out_4), .in_3(mux1_2_out_4), .in_1(S2), .out_4(L_0));
  \nor  nor_2 (.in_1(S2), .out_2(nor_2_out_2));
  MUX1 mux1_6 (.in_2(mux1_3_out_4), .in_3(mux1_4_out_4), .in_1(nor_2_out_2), .out_4(L_1));
endmodule

module \and  (
  input  in_1,
  input  in_2,
  output out_3
);

  wire transistor_2_out;

  Transistor transistor_1 (.in(1'b0), .out(out_3), .gate(in_2));
  Transistor #(.\type ("n")) transistor_2 (.in(1'b1), .out(transistor_2_out), .gate(in_1));
  Transistor #(.\type ("n")) transistor_3 (.in(transistor_2_out), .out(out_3), .gate(in_2));
  Transistor transistor_4 (.in(1'b0), .out(out_3), .gate(in_1));
endmodule

module \or  (
  input  in_1,
  input  in_2,
  output out_3
);

  wire transistor_4_out;

  Transistor #(.\type ("n")) transistor_1 (.in(1'b1), .out(out_3), .gate(in_1));
  Transistor #(.\type ("n")) transistor_2 (.in(1'b1), .out(out_3), .gate(in_2));
  Transistor transistor_3 (.in(transistor_4_out), .out(out_3), .gate(in_1));
  Transistor transistor_4 (.in(1'b0), .out(transistor_4_out), .gate(in_2));
endmodule

module \nor  (
  input  in_1,
  output out_2
);

  Transistor transistor_1 (.in(1'b1), .out(out_2), .gate(in_1));
  Transistor #(.\type ("n")) transistor_2 (.in(1'b0), .out(out_2), .gate(in_1));
endmodule
