// Logisim project firstex.circ as structural Verilog: 5 circuits, main circuit main
module main (
  input  in_1,
  input  in_2,
  input  in_3,
  input  in_4,
  input  in_5,
  input  in_6,
  input  in_7,
  input  in_8,
  input  in_9,
  input  in_10,
  input  in_11,
  input  in_12,
  input  in_13,
  input  in_14,
  input  in_15,
  input  in_16,
  input  in_17,
  output out_18,
  output out_19,
  output out_20,
  output out_21,
  output out_22,
  output out_23,
  output out_24,
  output out_25,
  output out_26
);

  wire four_add_1_out_14;

  four_add four_add_1 (
    .b1(in_10), .a1(in_2), .b2(in_11), .a2(in_3), .b3(in_12), .a3(in_4), .b4(in_13), .a4(in_5), .c1(out_18),
    .c2(out_19), .c3(out_20), .c4(out_21), .out_14(four_add_1_out_14), .in_1(in_1));
  four_add four_add_2 (
    .b1(in_14), .a1(in_6), .b2(in_15), .a2(in_7), .b3(in_16), .a3(in_8), .b4(in_17), .a4(in_9), .c1(out_22),
    .c2(out_23), .c3(out_24), .c4(out_25), .out_14(out_26), .in_1(four_add_1_out_14));
endmodule

module my_XOR (
  input  in_1,
  input  in_2,
  output out_3
);

  wire and_1_out, and_2_out, not_1_out, not_2_out;

  not not_1 (not_1_out, in_1);
  not not_2 (not_2_out, in_2);
  and and_1 (and_1_out, not_1_out, not_1_out, in_2);
  and and_2 (and_2_out, in_1, not_2_out);
  or or_1 (out_3, and_1_out, and_2_out);
endmodule

module HA (
  input  in_1,
  input  in_2,
  output \当前位 ,
  output \进位 
);

  my_XOR my_xor_1 (.in_1(in_1), .in_2(in_2), .out_3(\当前位 ));
  and and_1 (\进位 , in_1, in_1, in_2);
endmodule

module AA (
  input  S,
  input  ai,
  input  bi,
  output ci,
  output Si
);

  wire \ha_1_当前位 , \ha_1_进位 , \ha_2_进位 ;

  HA ha_1 (.in_1(ai), .in_2(bi), .\当前位 (\ha_1_当前位 ), .\进位 (\ha_1_进位 ));
  HA ha_2 (.in_1(S), .in_2(\ha_1_当前位 ), .\当前位 (ci), .\进位 (\ha_2_进位 ));
  or or_1 (Si, \ha_2_进位 , \ha_1_进位 );
endmodule

module four_add (
  input  in_1,
  input  b1,
  input  a1,
  input  b2,
  input  a2,
  input  b3,
  input  a3,
  input  b4,
  input  a4,
  output c1,
  output c2,
  output c3,
  output c4,
  output out_14
);

  wire aa_1_si, aa_2_si, aa_3_si;

  AA aa_1 (.S(in_1), .ai(a1), .bi(b1), .ci(c1), .Si(aa_1_si));
  AA aa_2 (.S(aa_1_si), .ai(a2), .bi(b2), .ci(c2), .Si(aa_2_si));
  AA aa_3 (.S(aa_2_si), .ai(a3), .bi(b3), .ci(c3), .Si(aa_3_si));
  AA aa_4 (.S(aa_3_si), .ai(a4), .bi(b4), .ci(c4), .Si(out_14));
endmodule
