// Logisim project shiyan.circ as structural Verilog: 4 circuits, main circuit main
module main (
  input  in_1,
  input  [3:0] in_2,
  input  in_3,
  input  [1:0] in_4,
  input  in_5,
  input  in_6,
  input  [1:0] in_7,
  input  in_8,
  input  in_9,
  input  [2:0] in_10,
  input  in_11,
  input  [2:0] in_12,
  input  [7:0] in_13,
  output out_14,
  output [3:0] out_15,
  output [2:0] out_16,
  output [2:0] out_17,
  output [3:0] out_18,
  output [3:0] out_19,
  output [5:0] out_20,
  output [1:0] out_21,
  output [3:0] out_22,
  output [3:0] out_23,
  output [1:0] out_24,
  output [1:0] out_25,
  output [1:0] out_26,
  output [1:0] out_27
);

  wire button_1_out, undriven;
  wire [1:0] and_1_out;
  wire [2:2] or_1_out;

  Button button_1 (.out(button_1_out));
  // Probe on in_2
  assign and_1_out = in_4 & in_7;  // AND_Gate and_1, 2 bits wide
  or or_1 (or_1_out[2], in_9, in_11);
  // Probe on in_2
  // Probe on in_2
  // Probe on in_2
  LED led_1 (.in(button_1_out));
  // Probe on in_2
  assign out_17 = ~{or_1_out[2], and_1_out};  // NOT_Gate not_1, 3 bits wide
  // Probe on {or_1_out[2], and_1_out}
  \半加器  \u_半加器_1  ();  // open: a, b, sum, cout
  nand nand_1 (in_5, 1'b1, in_3, undriven, in_6, in_12[0]);
  // Pins of 1 and 3 bits meet at in_12

  assign in_8 = in_6;
  assign out_14 = in_1;
  assign out_15 = in_2;
  assign out_16 = in_10;
  assign out_18 = in_13[3:0];
  assign out_19 = in_13[7:4];
  assign out_20 = in_13[7:2];
  assign out_21 = in_13[1:0];
  assign out_22 = in_13[7:4];
  assign out_23 = in_13[3:0];
  assign out_24 = in_13[1:0];
  assign out_25 = in_13[3:2];
  assign out_26 = in_13[5:4];
  assign out_27 = in_13[7:6];

  // Notes on the sheet:
  //   二进制
  //   八进制
  //   无符号十进制
  //   有符号十进制
  //   十六进制
endmodule

module \半加器  (
  input  a,
  input  b,
  output sum,
  output cout
);

  xor xor_1 (sum, a, b);
  and and_1 (cout, a, b);
endmodule

module \全加器  (
  input  in_1,
  input  in_2,
  input  in_3,
  output out_4,
  output out_5
);

  wire \半加器_1_cout , \半加器_1_sum , \半加器_2_cout ;

  \半加器  \u_半加器_1  (.a(in_1), .b(in_2), .sum(\半加器_1_sum ), .cout(\半加器_1_cout ));
  \半加器  \u_半加器_2  (.a(\半加器_1_sum ), .b(in_3), .sum(out_4), .cout(\半加器_2_cout ));
  or or_1 (out_5, \半加器_2_cout , \半加器_1_cout );
endmodule

module name (
);

  DotMatrix #(.matrixcols(16), .matrixrows(16)) dotmatrix_1 (
    .col0({16{1'b0}}), .col1(16'h7fff), .col2(16'h7fff), .col3(16'h7718), .col4(16'h7ffc), .col5(16'heff),
    .col6(16'h1fff), .col7(16'h7ffb), .col8(16'hf8c3), .col9(16'h5fff), .col10(16'h1fff), .col11(16'h18f0),
    .col12(16'h18fc), .col13(16'h18fe), .col14(16'h18df), .col15(16'h6));
  DotMatrix #(.matrixcols(16), .matrixrows(16)) dotmatrix_2 (
    .col0(16'h600), .col1(16'h660f), .col2(16'h7fff), .col3(16'h777f), .col4(16'h3138), .col5(16'h3ff8),
    .col6(16'h3ff8), .col7(16'h3030), .col8(16'h3ff8), .col9(16'h3fd8), .col10(16'hfcdb), .col11(16'hffdb),
    .col12(16'h7fdb), .col13(16'h3fdf), .col14(16'h3fff), .col15(16'he0));
  DotMatrix #(.matrixcols(16), .matrixrows(16)) dotmatrix_3 (
    .col0(16'h307), .col1(16'hf77), .col2(16'h3ff6), .col3(16'h7ffe), .col4(16'h7fee), .col5(16'he6c),
    .col6(16'h3b6c), .col7(16'h3bff), .col8(16'h3bff), .col9(16'h7fde), .col10(16'h7fde), .col11(16'h7fde),
    .col12(16'h7fde), .col13(16'h3fff), .col14(16'h3bff), .col15(16'h2300));
endmodule
