// Logisim project 实验3.circ as structural Verilog: 11 circuits, main circuit main
module main (
  input  in_1,
  input  in_2,
  input  in_3,
  input  in_4,
  output out_5,
  output out_6,
  output out_7,
  output out_8,
  output out_9
);

  wire clock_1_out, nand_1_out, nand_2_out, not_1_out, undriven;

  Clock clock_1 (.out(clock_1_out));
  \D触发器  \d触发器_1  (.D(in_4), .clk(clock_1_out), .Q(out_8));  // open: out_4
  not not_1 (not_1_out, in_1);
  nand nand_1 (nand_1_out, not_1_out, in_2);
  nand nand_2 (nand_2_out, in_2, in_1);
  nand nand_3 (out_5, nand_1_out, out_6);
  nand nand_4 (out_6, out_5, nand_2_out);
  \D锁  \d锁_1  (.D(in_3), .clk(undriven), .out_3(out_9), .Q(out_7));
endmodule

module \D锁  (
  input  D,
  input  clk,
  output out_3,
  output Q
);

  wire nand_1_out, nand_2_out, not_1_out;

  not not_1 (not_1_out, D);
  nand nand_1 (nand_1_out, not_1_out, clk);
  nand nand_2 (nand_2_out, clk, D);
  nand nand_3 (out_3, nand_1_out, Q);
  nand nand_4 (Q, out_3, nand_2_out);
endmodule

module \D触发器  (
  input  D,
  input  clk,
  output Q,
  output out_4
);

  wire \d锁_1_q , not_1_out;

  not not_1 (not_1_out, clk);
  \D锁  \d锁_1  (.D(D), .clk(not_1_out), .Q(\d锁_1_q ));  // open: out_3
  \D锁  \d锁_2  (.D(\d锁_1_q ), .clk(clk), .out_3(out_4), .Q(Q));
endmodule

module T1 (
  input  S,
  input  R,
  output out_3,
  output out_4
);

  nand nand_1 (out_3, S, out_4);
  nand nand_2 (out_4, out_3, R);
endmodule

module T2 (
  input  \D输入 ,
  input  in_2,
  input  rset,
  output out_4
);

  wire \d触发器_1_q , \d触发器_2_q , not_1_out;

  not not_1 (not_1_out, rset);
  \D触发器  \d触发器_1  (.D(\D输入 ), .clk(in_2), .Q(\d触发器_1_q ));  // open: out_4
  \D触发器  \d触发器_2  (.D(not_1_out), .clk(in_2), .Q(\d触发器_2_q ));  // open: out_4
  or or_1 (out_4, \d触发器_1_q , \d触发器_2_q );
endmodule

module \同步复位触发器  (
  input  D,
  input  reset,
  input  clk,
  output Q
);

  wire and_1_out;

  and and_1 (and_1_out, D, reset);
  \D触发器  \d触发器_1  (.D(and_1_out), .clk(clk), .Q(Q));  // open: out_4
endmodule

module \异步复位触发器  (
  input  D,
  input  clk,
  input  reset,
  output Q
);

  wire nand_1_out, nand_2_out, nand_3_out, nand_4_out, nand_5_out, nand_6_out, nand_7_out, not_1_out,
       not_2_out, not_3_out;

  not not_1 (not_1_out, D);
  not not_2 (not_2_out, clk);
  nand nand_1 (nand_1_out, not_1_out, not_2_out);
  nand nand_2 (nand_2_out, not_2_out, D, reset);
  nand nand_3 (nand_3_out, nand_1_out, reset, nand_4_out);
  nand nand_4 (nand_4_out, nand_3_out, nand_2_out);
  not not_3 (not_3_out, nand_4_out);
  nand nand_5 (nand_5_out, not_3_out, clk);
  nand nand_6 (nand_6_out, clk, nand_4_out, reset);
  nand nand_7 (nand_7_out, nand_5_out, reset, Q);
  nand nand_8 (Q, nand_7_out, nand_6_out);
endmodule

module \_4bit计数器  (
  input  in_1,
  input  reset,
  output [3:0] out_3
);

  wire [3:0] adder_1_out;

  Adder #(.width(4)) adder_1 (.a(out_3), .b(4'b0001), .out(adder_1_out));  // open: cin, cout
  \异步复位触发器  \u_异步复位触发器_1  (.D(adder_1_out[0]), .clk(reset), .reset(in_1), .Q(out_3[0]));
  \异步复位触发器  \u_异步复位触发器_2  (.D(adder_1_out[1]), .clk(reset), .reset(in_1), .Q(out_3[1]));
  \异步复位触发器  \u_异步复位触发器_3  (.D(adder_1_out[2]), .clk(reset), .reset(in_1), .Q(out_3[2]));
  \异步复位触发器  \u_异步复位触发器_4  (.D(adder_1_out[3]), .clk(reset), .reset(in_1), .Q(out_3[3]));

  // Notes on the sheet:
  //   output
endmodule

module \减法计数器  (
  input  [3:0] in_1,
  input  clk,
  input  reset,
  output [3:0] \output 
);

  wire or_1_out;
  wire [3:0] multiplexer_1_out, subtractor_1_out;

  Subtractor #(.width(4)) subtractor_1 (.a(\output ), .b(4'b0001), .out(subtractor_1_out));  // open: bin, bout
  Multiplexer #(.width(4)) multiplexer_1 (
    .in0(in_1), .in1(subtractor_1_out), .out(multiplexer_1_out), .sel(or_1_out));  // open: en
  or or_1 (or_1_out, \output [3], \output [0], \output [1], \output [2]);
  T2 t2_1 (.\D输入 (multiplexer_1_out[0]), .in_2(clk), .rset(reset), .out_4(\output [0]));
  \同步复位触发器  \u_同步复位触发器_1  (.D(reset), .reset(multiplexer_1_out[1]), .clk(clk), .Q(\output [1]));
  \同步复位触发器  \u_同步复位触发器_2  (.D(reset), .reset(multiplexer_1_out[2]), .clk(clk), .Q(\output [2]));
  T2 t2_2 (.\D输入 (multiplexer_1_out[3]), .in_2(clk), .rset(reset), .out_4(\output [3]));

  // Notes on the sheet:
  //   同步减法计数器
endmodule

module T4 (
  input  [3:0] in_1,
  input  in_2,
  output [3:0] out_3
);

  wire clock_1_out, or_1_out;
  wire [3:0] multiplexer_1_out, subtractor_1_out;

  Subtractor #(.width(4)) subtractor_1 (.a(out_3), .b(4'b0001), .out(subtractor_1_out));  // open: bin, bout
  Multiplexer #(.width(4)) multiplexer_1 (
    .in0(in_1), .in1(subtractor_1_out), .out(multiplexer_1_out), .sel(or_1_out));  // open: en
  Clock clock_1 (.out(clock_1_out));
  or or_1 (or_1_out, out_3[3], out_3[0], out_3[1], out_3[2]);
  T2 t2_1 (.\D输入 (multiplexer_1_out[0]), .in_2(clock_1_out), .rset(in_2), .out_4(out_3[0]));
  \同步复位触发器  \u_同步复位触发器_1  (.D(in_2), .reset(multiplexer_1_out[1]), .clk(clock_1_out), .Q(out_3[1]));
  \同步复位触发器  \u_同步复位触发器_2  (.D(in_2), .reset(multiplexer_1_out[2]), .clk(clock_1_out), .Q(out_3[2]));
  T2 t2_2 (.\D输入 (multiplexer_1_out[3]), .in_2(clock_1_out), .rset(in_2), .out_4(out_3[3]));

  // Notes on the sheet:
  //   同步减法计数器
endmodule

module T5 (
  input  reset,
  input  D,
  input  clk,
  output Q
);

  wire and_1_out, not_1_out;

  not not_1 (not_1_out, reset);
  and and_1 (and_1_out, not_1_out, D);
  \D触发器  \d触发器_1  (.D(and_1_out), .clk(clk), .Q(Q));  // open: out_4
endmodule
