// Logisim project 实验2.circ as structural Verilog
module \真值表生成  (
  input  I4,
  input  I3,
  input  I2,
  input  I1,
  output O4,
  output O3,
  output O2,
  output O1
);

  wire and_2_out, not_3_out, not_4_out;

  not not_1 (O4, I2);
  and and_1 (O3, I2, I1);
  not not_2 (O2, I3);
  not not_3 (not_3_out, I4);
  not not_4 (not_4_out, I1);
  and and_2 (and_2_out, not_3_out, I2);
  or or_1 (O1, not_4_out, and_2_out, I3);
endmodule

module \表达式生成化简1  (
  input  i0,
  input  i1,
  input  i2,
  input  i3,
  input  i4,
  input  i5,
  input  i6,
  input  i7,
  output y0,
  output y1,
  output y2
);

  wire and_1_out, and_2_out, and_3_out, and_4_out, and_5_out, and_6_out, and_7_out, and_8_out, and_9_out,
       not_1_out, not_2_out, not_3_out, not_4_out, not_5_out, not_6_out, not_7_out, not_8_out, not_9_out,
       not_10_out, not_11_out, not_12_out, not_13_out, not_14_out, not_15_out, not_16_out, not_17_out,
       not_18_out, not_19_out, not_20_out, not_21_out, not_22_out;

  not not_1 (not_1_out, i6);
  not not_2 (not_2_out, i4);
  not not_3 (not_3_out, i6);
  not not_4 (not_4_out, i2);
  not not_5 (not_5_out, i4);
  not not_6 (not_6_out, i6);
  not not_7 (not_7_out, i7);
  not not_8 (not_8_out, i7);
  not not_9 (not_9_out, i6);
  not not_10 (not_10_out, i5);
  not not_11 (not_11_out, i4);
  not not_12 (not_12_out, i7);
  not not_13 (not_13_out, i6);
  not not_14 (not_14_out, i5);
  not not_15 (not_15_out, i4);
  not not_16 (not_16_out, i3);
  not not_17 (not_17_out, i7);
  not not_18 (not_18_out, i7);
  not not_19 (not_19_out, i6);
  not not_20 (not_20_out, i7);
  not not_21 (not_21_out, i6);
  not not_22 (not_22_out, i5);
  and and_1 (and_1_out, i5, not_1_out);
  and and_2 (and_2_out, i3, not_2_out, not_3_out);
  and and_3 (and_3_out, i1, not_4_out, not_5_out, not_6_out);
  and and_4 (and_4_out, not_7_out, i6);
  and and_5 (and_5_out, not_8_out, not_9_out, not_10_out, not_11_out, i3);
  and and_6 (and_6_out, not_12_out, not_13_out, not_14_out, not_15_out, not_16_out, i2);
  and and_7 (and_7_out, not_17_out, i6);
  and and_8 (and_8_out, not_18_out, not_19_out, i5);
  and and_9 (and_9_out, not_20_out, not_21_out, not_22_out, i4);
  or or_1 (y0, i7, and_1_out, and_2_out, and_3_out);
  or or_2 (y1, i7, and_4_out, and_5_out, and_6_out);
  or or_3 (y2, i7, and_7_out, and_8_out, and_9_out);
endmodule

module \表达式化简2  (
  input  i0,
  input  i1,
  input  i2,
  input  i3,
  input  i4,
  input  i5,
  input  i6,
  input  i7,
  output y0,
  output y1,
  output y2
);

  wire not_1_out, not_2_out, not_3_out, not_4_out, not_5_out, or_1_out, or_2_out, or_3_out, or_5_out,
       or_6_out, or_7_out, or_8_out;

  not not_1 (not_1_out, i6);
  not not_2 (not_2_out, i4);
  not not_3 (not_3_out, i2);
  or or_1 (or_1_out, i2, i3, i6, i7);
  not not_4 (not_4_out, i5);
  or or_2 (or_2_out, not_4_out, i6, i7);
  not not_5 (not_5_out, i4);
  or or_3 (or_3_out, not_5_out, i6, i7);
  or or_4 (y2, i4, i5, i6, i7);
  or or_5 (or_5_out, i1, i3, i5, i7);
  or or_6 (or_6_out, not_1_out, i7);
  or or_7 (or_7_out, not_2_out, i5, i7);
  or or_8 (or_8_out, not_3_out, i3, i5, i7);
  and and_1 (y1, or_1_out, or_2_out, or_3_out);
  and and_2 (y0, or_5_out, or_6_out, or_7_out, or_8_out);
endmodule

module \表达式生成  (
  input  i0,
  input  i1,
  input  i2,
  input  i3,
  input  i4,
  input  i5,
  input  i6,
  input  i7,
  output y0,
  output y1,
  output y2
);

  wire and_1_out, and_2_out, and_3_out, and_4_out, and_5_out, and_6_out, and_7_out, and_8_out, and_9_out,
       not_1_out, not_2_out, not_3_out, not_4_out, not_5_out, not_6_out, not_7_out, not_8_out, not_9_out,
       not_10_out, not_11_out, not_12_out, not_13_out, not_14_out, not_15_out, not_16_out, not_17_out,
       not_18_out, not_19_out, not_20_out, not_21_out, not_22_out, not_23_out, not_24_out, not_25_out,
       not_26_out, not_27_out, not_28_out;

  not not_1 (not_1_out, i7);
  not not_2 (not_2_out, i6);
  not not_3 (not_3_out, i7);
  not not_4 (not_4_out, i6);
  not not_5 (not_5_out, i5);
  not not_6 (not_6_out, i4);
  not not_7 (not_7_out, i7);
  not not_8 (not_8_out, i6);
  not not_9 (not_9_out, i5);
  not not_10 (not_10_out, i4);
  not not_11 (not_11_out, i3);
  not not_12 (not_12_out, i2);
  not not_13 (not_13_out, i7);
  not not_14 (not_14_out, i7);
  not not_15 (not_15_out, i6);
  not not_16 (not_16_out, i5);
  not not_17 (not_17_out, i4);
  not not_18 (not_18_out, i7);
  not not_19 (not_19_out, i6);
  not not_20 (not_20_out, i5);
  not not_21 (not_21_out, i4);
  not not_22 (not_22_out, i3);
  not not_23 (not_23_out, i7);
  not not_24 (not_24_out, i7);
  not not_25 (not_25_out, i6);
  not not_26 (not_26_out, i7);
  not not_27 (not_27_out, i6);
  not not_28 (not_28_out, i5);
  and and_1 (and_1_out, not_1_out, not_2_out, i5);
  and and_2 (and_2_out, not_3_out, not_4_out, not_5_out, not_6_out, i3);
  and and_3 (and_3_out, not_7_out, not_8_out, not_9_out, not_10_out, not_11_out, not_12_out, i1);
  and and_4 (and_4_out, not_13_out, i6);
  and and_5 (and_5_out, not_14_out, not_15_out, not_16_out, not_17_out, i3);
  and and_6 (and_6_out, not_18_out, not_19_out, not_20_out, not_21_out, not_22_out, i2);
  and and_7 (and_7_out, not_23_out, i6);
  and and_8 (and_8_out, not_24_out, not_25_out, i5);
  and and_9 (and_9_out, not_26_out, not_27_out, not_28_out, i4);
  or or_1 (y0, i7, and_1_out, and_2_out, and_3_out);
  or or_2 (y1, i7, and_4_out, and_5_out, and_6_out);
  or or_3 (y2, i7, and_7_out, and_8_out, and_9_out);
endmodule

module T1 (
  input  Ci1,
  input  Ai,
  input  Bi,
  output Si,
  output Ci
);

  wire and_1_out, and_2_out, and_3_out, and_4_out, and_5_out, and_6_out, and_7_out, not_1_out, not_2_out,
       not_3_out, not_4_out, not_5_out, not_6_out;

  not not_1 (not_1_out, Ci1);
  not not_2 (not_2_out, Ai);
  not not_3 (not_3_out, Ci1);
  not not_4 (not_4_out, Bi);
  not not_5 (not_5_out, Ai);
  not not_6 (not_6_out, Bi);
  and and_1 (and_1_out, not_1_out, not_2_out, Bi);
  and and_2 (and_2_out, not_3_out, Ai, not_4_out);
  and and_3 (and_3_out, Ci1, not_5_out, not_6_out);
  and and_4 (and_4_out, Ci1, Ai, Bi);
  and and_5 (and_5_out, Ai, Bi);
  or or_1 (Ci, and_5_out, and_6_out, and_7_out);
  and and_6 (and_6_out, Ci1, Bi);
  and and_7 (and_7_out, Ci1, Ai);
  or or_2 (Si, and_1_out, and_2_out, and_3_out, and_4_out);

  // Notes on the sheet:
  //   PB21000224 陈鸿绪
endmodule

module T2 (
  input  G1,
  input  G2,
  input  G3,
  input  A2,
  input  A1,
  input  A0,
  output Y7,
  output Y6,
  output Y5,
  output Y4,
  output Y3,
  output Y2,
  output Y1,
  output Y0
);

  wire not_1_out, not_2_out, not_3_out, not_4_out, not_5_out, not_6_out, not_7_out, not_8_out, not_9_out,
       not_10_out, not_11_out, not_12_out, not_13_out, not_14_out, not_15_out, not_16_out, not_17_out,
       not_18_out, not_19_out, not_20_out, not_21_out, not_22_out, not_23_out, not_24_out, not_25_out,
       not_26_out, not_27_out, not_28_out, not_29_out, not_30_out;

  not not_1 (not_1_out, G1);
  not not_2 (not_2_out, A2);
  not not_3 (not_3_out, A1);
  not not_4 (not_4_out, A0);
  not not_5 (not_5_out, G2);
  not not_6 (not_6_out, G3);
  not not_7 (not_7_out, A0);
  not not_8 (not_8_out, G2);
  not not_9 (not_9_out, G3);
  not not_10 (not_10_out, A1);
  not not_11 (not_11_out, G2);
  not not_12 (not_12_out, G3);
  not not_13 (not_13_out, A1);
  not not_14 (not_14_out, A0);
  not not_15 (not_15_out, G2);
  not not_16 (not_16_out, G3);
  not not_17 (not_17_out, A2);
  not not_18 (not_18_out, G2);
  not not_19 (not_19_out, G3);
  not not_20 (not_20_out, A2);
  not not_21 (not_21_out, A0);
  not not_22 (not_22_out, G2);
  not not_23 (not_23_out, G3);
  not not_24 (not_24_out, A2);
  not not_25 (not_25_out, A1);
  not not_26 (not_26_out, G2);
  not not_27 (not_27_out, G3);
  not not_28 (not_28_out, A2);
  not not_29 (not_29_out, A1);
  not not_30 (not_30_out, A0);
  or or_1 (Y7, not_1_out, not_2_out, not_3_out, not_4_out, G3, G2);
  nand nand_1 (Y6, G1, not_5_out, not_6_out, A2, A1, not_7_out);
  nand nand_2 (Y5, G1, not_8_out, not_9_out, A2, not_10_out, A0);
  nand nand_3 (Y4, G1, not_11_out, not_12_out, A2, not_13_out, not_14_out);
  nand nand_4 (Y3, G1, not_15_out, not_16_out, not_17_out, A1, A0);
  nand nand_5 (Y2, G1, not_18_out, not_19_out, not_20_out, A1, not_21_out);
  nand nand_6 (Y1, G1, not_22_out, not_23_out, not_24_out, not_25_out, A0);
  nand nand_7 (Y0, G1, not_26_out, not_27_out, not_28_out, not_29_out, not_30_out);

  // Notes on the sheet:
  //   PB21000224 陈鸿绪
endmodule

module MUX (
  input  sel,
  input  b,
  input  a,
  output out
);

  wire and_1_out, and_2_out, not_1_out;

  and and_1 (and_1_out, sel, b);
  not not_1 (not_1_out, sel);
  and and_2 (and_2_out, not_1_out, a);
  or or_1 (out, and_1_out, and_2_out);

  // Notes on the sheet:
  //   PB210000224 陈鸿绪
endmodule

module MUX4_1 (
  input  sel1,
  input  sel0,
  input  d,
  input  b,
  input  c,
  input  a,
  output out
);

  wire mux_1_out, mux_2_out;

  MUX mux_1 (.sel(sel1), .b(d), .a(b), .out(mux_1_out));
  MUX mux_2 (.sel(sel1), .b(c), .a(a), .out(mux_2_out));
  MUX mux_3 (.sel(sel0), .b(mux_1_out), .a(mux_2_out), .out(out));

  // Notes on the sheet:
  //   PB21000224 陈鸿绪
endmodule

module T6 (
  input  a,
  input  b,
  input  c,
  output s1,
  output s2
);

  wire and_1_out, and_2_out, and_3_out, and_4_out, and_5_out, and_6_out, and_7_out, and_8_out, not_1_out,
       not_2_out, not_3_out, not_4_out, not_5_out, not_6_out, not_7_out, not_8_out, not_9_out, not_10_out,
       not_11_out, not_12_out;

  not not_1 (not_1_out, a);
  not not_2 (not_2_out, b);
  not not_3 (not_3_out, a);
  not not_4 (not_4_out, c);
  not not_5 (not_5_out, b);
  not not_6 (not_6_out, c);
  not not_7 (not_7_out, a);
  not not_8 (not_8_out, b);
  not not_9 (not_9_out, c);
  not not_10 (not_10_out, a);
  not not_11 (not_11_out, b);
  not not_12 (not_12_out, c);
  and and_1 (and_1_out, not_1_out, not_2_out, c);
  and and_2 (and_2_out, not_3_out, b, not_4_out);
  and and_3 (and_3_out, a, not_5_out, not_6_out);
  and and_4 (and_4_out, a, b, c);
  and and_5 (and_5_out, not_7_out, b, c);
  and and_6 (and_6_out, a, not_8_out, c);
  and and_7 (and_7_out, a, b, not_9_out);
  and and_8 (and_8_out, not_10_out, not_11_out, not_12_out);
  or or_1 (s1, and_1_out, and_2_out, and_3_out, and_4_out);
  or or_2 (s2, and_5_out, and_6_out, and_7_out, and_8_out);

  // Notes on the sheet:
  //   PB21000224 陈鸿绪
endmodule
